# Fritzing sketch arduino_diagramm (saved by Fritzing 0.9.2b)
perfboards: 1

parts:
  DIN1 = DIN-5 jack (MIDI) [package=THT]
  Bauteil1 = Arduino Mega 2560 (Rev3)
  R1 = Resistor [tolerance=±5% resistance=220 package=THT]
  R2 = Resistor [tolerance=±5% resistance=1k package=THT]
  S1 = Pushbutton [package="[THT]"]
  R3 = Rotary Potentiometer (Small) [maximum_resistance=100kΩ package=THT]
  Bauteil3 = Arduino Nano (Rev3.0)
  R4 = Resistor [tolerance=±5% resistance=1k package=THT]
  R5 = Resistor [tolerance=±5% resistance=1k package=THT]  # not connected
  R6 = Resistor [tolerance=±5% resistance=1k package=THT]  # not connected
  R7 = Resistor [tolerance=±5% resistance=1k package=THT]  # not connected
  R8 = Resistor [tolerance=±5% resistance=1k package=THT]  # not connected
  R9 = Resistor [tolerance=±5% resistance=1k package=THT]  # not connected
  R10 = Resistor [tolerance=±5% resistance=1k package=THT]  # not connected
  R11 = Resistor [tolerance=±5% resistance=100 package=THT]  # not connected
  R12 = Resistor [tolerance=±5% resistance=100 package=THT]  # not connected
  R13 = Resistor [tolerance=±5% resistance=100 package=THT]  # not connected
  R14 = Resistor [tolerance=±5% resistance=100 package=THT]  # not connected
  LED1 = LED - 5mm [color="Red (633nm)" package="5 mm [THT]"]  # not connected
  S2 = Pushbutton [package="[THT]"]
  R15 = Rotary Potentiometer (Small) [maximum_resistance=100kΩ package=THT]  # not connected

nets:
  N1: DIN1.5, Bauteil1.D1_TX0
  N2: DIN1.2, Bauteil1.GND, R2.Pin_0, R3.leg2
  N3: Bauteil1.A0, R3.wiper
  N4: Bauteil1.5V, R1.Pin_1, R3.leg1
  N5: Bauteil1.D4_PWM, R2.Pin_1, S1.Pin_3, S1.Pin_4
  N6: Bauteil3.GND, R4.Pin_1
  N7: Bauteil3.5V, S2.Pin_1, S2.Pin_2
